// Logisim project Lab01.circ as structural Verilog: 1 circuit, main circuit main
module main (
  input  in_1,
  input  in_2,
  input  in_3,
  input  in_4,
  input  in_5,
  input  in_6,
  input  in_7,
  input  in_8,
  input  in_9,
  input  in_10
);

  wire and_1_out, and_2_out, and_3_out, and_4_out, nand_1_out, not_1_out, or_1_out, xor_1_out, xor_2_out,
       xor_3_out;

  not not_1 (not_1_out, in_3);
  and and_1 (and_1_out, in_1, in_2);
  LED led_1 (.in(not_1_out));
  nand nand_1 (nand_1_out, in_4, in_5);
  LED led_2 (.in(and_1_out));
  LED led_3 (.in(nand_1_out));
  xor xor_1 (xor_1_out, in_7, in_8);
  and and_2 (and_2_out, in_7, in_8);
  xor xor_2 (xor_2_out, in_9, in_10);
  and and_3 (and_3_out, in_10, in_9);
  LED led_4 (.in(xor_2_out));
  LED led_5 (.in(and_3_out));
  xor xor_3 (xor_3_out, in_6, xor_1_out);
  and and_4 (and_4_out, in_6, xor_1_out);
  LED led_6 (.in(xor_3_out));
  or or_1 (or_1_out, and_4_out, and_2_out);
  LED led_7 (.in(or_1_out));
endmodule
