// Logisim project lab02.circ as structural Verilog: 1 circuit, main circuit main
module main (
  input  in_1,
  input  in_2,
  input  in_3,
  input  in_4,
  input  in_5,
  input  in_6,
  input  in_7,
  input  in_8,
  input  in_9,
  input  in_10,
  input  in_11,
  input  in_12,
  input  in_13,
  input  in_14,
  input  in_15
);

  wire and_1_out, and_2_out, and_3_out, and_4_out, and_5_out, and_6_out, and_7_out, and_8_out, and_9_out,
       clock_1_out, clock_2_out, nand_1_out, nand_2_out, nand_3_out, nand_4_out, nand_5_out, nand_6_out,
       nor_1_out, nor_2_out, nor_3_out, nor_4_out, not_1_out, or_1_out, or_2_out, or_3_out, xor_1_out,
       xor_2_out, xor_3_out, xor_4_out, xor_5_out, xor_6_out, xor_7_out;

  Clock clock_1 (.out(clock_1_out));
  Clock clock_2 (.out(clock_2_out));
  not not_1 (not_1_out, in_5);
  nor nor_1 (nor_1_out, in_3, nor_2_out);
  nor nor_2 (nor_2_out, nor_1_out, in_4);
  and and_1 (and_1_out, not_1_out, clock_1_out);
  and and_2 (and_2_out, clock_1_out, in_5);
  xor xor_1 (xor_1_out, in_10, in_11);
  xor xor_2 (xor_2_out, in_12, in_13);
  xor xor_3 (xor_3_out, in_14, in_15);
  nand nand_1 (nand_1_out, in_1, nand_2_out);
  nand nand_2 (nand_2_out, nand_1_out, in_2);
  nand nand_3 (nand_3_out, nand_6_out, in_6, clock_2_out);
  nand nand_4 (nand_4_out, clock_2_out, in_7, nand_5_out);
  xor xor_4 (xor_4_out, in_8, in_9);
  and and_3 (and_3_out, in_8, in_9);
  and and_4 (and_4_out, in_10, in_11);
  and and_5 (and_5_out, or_3_out, xor_2_out);
  and and_6 (and_6_out, in_12, in_13);
  and and_7 (and_7_out, xor_3_out, or_1_out);
  and and_8 (and_8_out, in_15, in_14);
  LED led_1 (.in(nor_1_out));
  LED led_2 (.in(nor_2_out));
  nor nor_3 (nor_3_out, and_1_out, nor_4_out);
  nor nor_4 (nor_4_out, nor_3_out, and_2_out);
  LED led_3 (.in(nor_4_out));
  LED led_4 (.in(nand_1_out));
  LED led_5 (.in(nand_2_out));
  LED led_6 (.in(nor_3_out));
  nand nand_5 (nand_5_out, nand_3_out, nand_6_out);
  nand nand_6 (nand_6_out, nand_5_out, nand_4_out);
  xor xor_5 (xor_5_out, and_3_out, xor_1_out);
  and and_9 (and_9_out, and_3_out, xor_1_out);
  xor xor_6 (xor_6_out, xor_2_out, or_3_out);
  or or_1 (or_1_out, and_5_out, and_6_out);
  xor xor_7 (xor_7_out, xor_3_out, or_1_out);
  or or_2 (or_2_out, and_7_out, and_8_out);
  or or_3 (or_3_out, and_9_out, and_4_out);
  LED led_7 (.in(nand_5_out));
  LED led_8 (.in(nand_6_out));
  LED led_9 (.in(xor_4_out));
  LED led_10 (.in(xor_5_out));
  LED led_11 (.in(xor_6_out));
  LED led_12 (.in(xor_7_out));
  LED led_13 (.in(or_2_out));
endmodule
