// Logisim project Lab03.circ as structural Verilog: 1 circuit, main circuit main
module main (
  input  in_1,
  input  in_2,
  input  in_3,
  input  in_4,
  input  in_5,
  input  in_6,
  input  in_7,
  input  in_8,
  input  in_9,
  input  in_10,
  input  in_11,
  input  in_12,
  input  in_13,
  input  in_14,
  input  in_15
);

  wire and_1_out, and_2_out, clock_1_out, clock_2_out, clock_3_out, clock_4_out, clock_5_out, clock_6_out,
       clock_7_out, d_ff_1_q, d_ff_2_q, d_ff_3_q, d_ff_4_q, j_k_ff_7_q, j_k_ff_8_q, j_k_ff_10_q, j_k_ff_11_q,
       j_k_ff_12_q, j_k_ff_14_q, j_k_ff_15_q, j_k_ff_16_q, j_k_ff_17_q;
  wire [2:0] d_ff_5_q, j_k_ff_1_q, j_k_ff_2_q, j_k_ff_9_q;

  Clock clock_1 (.out(clock_1_out));
  Clock clock_2 (.out(clock_2_out));
  Clock clock_3 (.out(clock_3_out));
  D_Flip_Flop d_ff_1 (.D(in_4), .clk(clock_3_out), .Q(d_ff_1_q), .reset(in_6));  // open: Qn, preset
  J_K_Flip_Flop #(.trigger("falling")) j_k_ff_1 (
    .J(in_8), .K(in_8), .clk(clock_1_out), .Q(j_k_ff_1_q[0]));  // open: Qn, preset, reset
  J_K_Flip_Flop j_k_ff_2 (.J(in_10), .K(in_10), .clk(clock_2_out), .Q(j_k_ff_2_q[0]));  // open: Qn, preset, reset
  LED led_1 (.in(d_ff_1_q));
  LED led_2 (.in(j_k_ff_1_q[0]));
  LED led_3 (.in(j_k_ff_2_q[0]));
  D_Flip_Flop d_ff_2 (.D(in_5), .clk(clock_3_out), .Q(d_ff_2_q), .reset(in_6));  // open: Qn, preset
  J_K_Flip_Flop #(.trigger("falling")) j_k_ff_3 (
    .J(in_8), .K(in_8), .clk(j_k_ff_1_q[0]), .Q(j_k_ff_1_q[1]));  // open: Qn, preset, reset
  J_K_Flip_Flop j_k_ff_4 (.J(in_10), .K(in_10), .clk(j_k_ff_2_q[0]), .Q(j_k_ff_2_q[1]));  // open: Qn, preset, reset
  LED led_4 (.in(d_ff_2_q));
  D_Flip_Flop d_ff_3 (.D(in_1), .clk(clock_3_out), .Q(d_ff_3_q), .reset(in_6));  // open: Qn, preset
  LED led_5 ();  // open: in
  LED led_6 ();  // open: in
  LED led_7 (.in(d_ff_3_q));
  J_K_Flip_Flop #(.trigger("falling")) j_k_ff_5 (
    .J(in_8), .K(in_8), .clk(j_k_ff_1_q[1]), .Q(j_k_ff_1_q[2]));  // open: Qn, preset, reset
  J_K_Flip_Flop j_k_ff_6 (.J(in_10), .K(in_10), .clk(j_k_ff_2_q[1]), .Q(j_k_ff_2_q[2]));  // open: Qn, preset, reset
  LED led_8 (.in(d_ff_4_q));
  D_Flip_Flop d_ff_4 (.D(in_3), .clk(clock_3_out), .Q(d_ff_4_q), .reset(in_6));  // open: Qn, preset
  LED led_9 (.in(j_k_ff_1_q[2]));
  LED led_10 (.in(j_k_ff_2_q[2]));
  Clock clock_4 (.out(clock_4_out));
  Clock clock_5 (.out(clock_5_out));
  Hex_Digit_Display hex_digit_display_1 (.value({in_11, j_k_ff_1_q}), .dp(j_k_ff_1_q[0]));
  Hex_Digit_Display hex_digit_display_2 (.value({in_14, j_k_ff_2_q}));  // open: dp
  Clock clock_6 (.out(clock_6_out));
  Clock clock_7 (.out(clock_7_out));
  Button button_1 ();  // open: out
  J_K_Flip_Flop #(.trigger("falling")) j_k_ff_7 (
    .J(in_2), .K(in_2), .clk(clock_4_out), .Q(j_k_ff_7_q));  // open: Qn, preset, reset
  J_K_Flip_Flop j_k_ff_8 (.J(in_7), .K(in_7), .clk(clock_5_out), .Q(j_k_ff_8_q));  // open: Qn, preset, reset
  LED led_11 (.in(j_k_ff_7_q));
  LED led_12 (.in(j_k_ff_8_q));
  J_K_Flip_Flop j_k_ff_9 (
    .J(in_9), .K(in_9), .clk(clock_6_out), .Q(j_k_ff_9_q[0]), .reset(and_1_out));  // open: Qn, preset
  J_K_Flip_Flop j_k_ff_10 (
    .J(in_13), .K(in_13), .clk(clock_7_out), .Q(j_k_ff_10_q), .reset(and_2_out));  // open: Qn, preset
  LED led_13 (.in(j_k_ff_10_q));
  J_K_Flip_Flop #(.trigger("falling")) j_k_ff_11 (
    .J(in_2), .K(in_2), .clk(j_k_ff_7_q), .Q(j_k_ff_11_q));  // open: Qn, preset, reset
  J_K_Flip_Flop j_k_ff_12 (.J(in_7), .K(in_7), .clk(j_k_ff_8_q), .Q(j_k_ff_12_q));  // open: Qn, preset, reset
  LED led_14 (.in(j_k_ff_9_q[0]));
  D_Flip_Flop d_ff_5 (.D(j_k_ff_10_q), .clk(clock_7_out), .Q(d_ff_5_q[0]));  // open: Qn, preset, reset
  LED led_15 (.in(j_k_ff_11_q));
  LED led_16 (.in(j_k_ff_12_q));
  J_K_Flip_Flop #(.trigger("falling")) j_k_ff_13 (
    .J(in_9), .K(in_9), .clk(j_k_ff_9_q[0]), .Q(j_k_ff_9_q[1]), .reset(and_1_out));  // open: Qn, preset
  J_K_Flip_Flop #(.trigger("falling")) j_k_ff_14 (
    .J(in_13), .K(in_13), .clk(j_k_ff_10_q), .Q(j_k_ff_14_q), .reset(and_2_out));  // open: Qn, preset
  J_K_Flip_Flop #(.trigger("falling")) j_k_ff_15 (
    .J(in_2), .K(in_2), .clk(j_k_ff_11_q), .Q(j_k_ff_15_q));  // open: Qn, preset, reset
  J_K_Flip_Flop j_k_ff_16 (.J(in_7), .K(in_7), .clk(j_k_ff_12_q), .Q(j_k_ff_16_q));  // open: Qn, preset, reset
  LED led_17 (.in(j_k_ff_9_q[1]));
  LED led_18 (.in(j_k_ff_14_q));
  LED led_19 (.in(j_k_ff_15_q));
  LED led_20 (.in(j_k_ff_16_q));
  J_K_Flip_Flop #(.trigger("falling")) j_k_ff_17 (
    .J(in_13), .K(in_13), .clk(j_k_ff_14_q), .Q(j_k_ff_17_q), .reset(and_2_out));  // open: Qn, preset
  D_Flip_Flop d_ff_6 (.D(j_k_ff_14_q), .clk(clock_7_out), .Q(d_ff_5_q[1]));  // open: Qn, preset, reset
  J_K_Flip_Flop #(.trigger("falling")) j_k_ff_18 (
    .J(in_9), .K(in_9), .clk(j_k_ff_9_q[1]), .Q(j_k_ff_9_q[2]), .reset(and_1_out));  // open: Qn, preset
  LED led_21 (.in(j_k_ff_9_q[2]));
  LED led_22 (.in(j_k_ff_17_q));
  and and_1 (and_1_out, j_k_ff_9_q[1], j_k_ff_9_q[2]);
  and and_2 (and_2_out, j_k_ff_14_q, j_k_ff_17_q);
  D_Flip_Flop d_ff_7 (.D(j_k_ff_17_q), .clk(clock_7_out), .Q(d_ff_5_q[2]));  // open: Qn, preset, reset
  Hex_Digit_Display hex_digit_display_3 (.value({in_12, j_k_ff_9_q}));  // open: dp
  Hex_Digit_Display hex_digit_display_4 (.value({in_15, d_ff_5_q}));  // open: dp
  // Pins of 1 and 4 bits meet at {in_11, j_k_ff_1_q}
endmodule
